# Fritzing sketch Hello_LCDFritzing (saved by Fritzing 0.9.3b)
breadboards: 1

parts:
  Part1 = Arduino Uno (Rev3)
  LCD1 = LCD screen
  U1 = POT [package=3362u]

nets:
  N1: Part1.D8, LCD1.E
  N2: Part1.D9_PWM, LCD1.DB4
  N3: Part1.D10_PWM/SS, LCD1.DB5
  N4: Part1.D11_PWM/MOSI, LCD1.DB6
  N5: Part1.D12/MISO, LCD1.DB7
  GND: Part1.GND, LCD1.VSS, LCD1.R/W, LCD1.LED-, U1.E
  N6: Part1.D7, LCD1.RS
  5V: Part1.5V, LCD1.VDD, LCD1.LED+, U1.A
  N7: LCD1.V0, U1.S
