# Fritzing sketch LCD_BackpackFritzing (saved by Fritzing 0.9.3b)
breadboards: 1

parts:
  Part1 = Arduino Uno (Rev3)
  LCD2 = LCD screen  # not connected
  S1 = Pushbutton [package="[SMD]"]

nets:
  N1: Part1.GND, Part1.D6_PWM, S1.Pin_3, S1.Pin_4
  N2: Part1.5V, S1.Pin_1, S1.Pin_2

notes:
  SDA
  SCL
