# Fritzing sketch Motor_ControlFritzing (saved by Fritzing 0.9.3b)
breadboards: 1

parts:
  Part1 = Arduino Uno (Rev3)
  VCC1 = Battery
  D1 = Diode [package=diode-1n4148]
  Q1 = NPN-Transistor [package="SOT-23 [SMD]"]
  R1 = Resistor [tolerance=±5% resistance=220 package=THT]
  U1 = POT [package=3362u]  # not connected
  M1 = DC Motor

nets:
  N1: Part1.D3_PWM, R1.Pin_1
  N2: Part1.GND, VCC1.-, Q1.2
  N3: VCC1.+, M1.pin_2
  N4: D1.C, M1.pin_1
  N5: Q1.0, R1.Pin_0
