# Fritzing sketch PhotointerrupterFritzing (saved by Fritzing 0.9.3b)
breadboards: 1

parts:
  Part1 = Arduino Uno (Rev3)
  LED1 = smd LED [color="Red (633nm)" package="0603 [SMD]"]
  R1 = Resistor [tolerance=±5% resistance=220 package="0402 [SMD]"]
  Q1 = PHOTOTRANSISTOR REFLECTIVE OBJECT SENSOR [package=qrb1114-side]

nets:
  N1: Part1.D3_PWM, Q1.E
  N2: Part1.D4, LED1.anode
  N3: Part1.5V, Q1.A, Q1.C, Q1.K
  N4: Part1.GND, R1.Pin_0
  N5: LED1.cathode, R1.Pin_1
