# Fritzing sketch PotentiometersFritzing (saved by Fritzing 0.9.3b)
breadboards: 1

parts:
  Part1 = Arduino Uno (Rev3)
  LCD2 = LCD screen  # not connected
  R1 = Rotary Potentiometer (Large) [maximum_resistance=100kΩ package=THT]
  LED1 = LEDs [package=led10mm]
  R2 = Resistor [tolerance=±5% resistance=220 package="0805 [SMD]"]

nets:
  N1: Part1.A3, R1.wiper
  N2: Part1.D5_PWM, LED1.C
  N3: Part1.5V, R1.leg2
  N4: Part1.GND, R1.leg1, R2.Pin_1
  N5: LED1.A, R2.Pin_0

notes:
  SDA
  SCL
